# Fritzing sketch Ambulance_circuit (saved by Fritzing 0.8.7b)

parts:
  MH-ET_LIVE_ESP32_DEVKIT1 = MH-ET LIVE ESP32 DEVKIT 38 pins
  LED2 = LED - 5mm [color="Blue (470nm)" package="5 mm [THT]"]
  LED3 = LED - 5mm [color="Green (555nm)" package="5 mm [THT]"]
  LED4 = LED - 5mm [color="Red (633nm)" package="5 mm [THT]"]
  J1 = Piezo Speaker
  J2 = Piezo Speaker
  S1 = Pushbutton [package=THT]
  S2 = Pushbutton [package=THT]
  S3 = Round Pushbutton
  Part1 = Lilypad Power Supply

nets:
  N1: MH-ET_LIVE_ESP32_DEVKIT1.IO12, J2.pin2
  N2: MH-ET_LIVE_ESP32_DEVKIT1.GND#58, S1.leg0
  N3: MH-ET_LIVE_ESP32_DEVKIT1.IO13, J1.pin2
  N4: MH-ET_LIVE_ESP32_DEVKIT1.5V, Part1.+
  N5: MH-ET_LIVE_ESP32_DEVKIT1.GND#64, LED4.cathode
  N6: MH-ET_LIVE_ESP32_DEVKIT1.IO19, LED2.anode
  N7: MH-ET_LIVE_ESP32_DEVKIT1.IO18, S2.leg1
  N8: MH-ET_LIVE_ESP32_DEVKIT1.IO5, S1.leg1
  N9: MH-ET_LIVE_ESP32_DEVKIT1.IO17, S3.leg1
  N10: MH-ET_LIVE_ESP32_DEVKIT1.IO16, LED3.anode
  N11: MH-ET_LIVE_ESP32_DEVKIT1.IO4, LED4.anode
  N12: J1.pin1, J2.pin1, S3.leg0, Part1.GND

custom parts:
  MH-ET LIVE ESP32 DEVKIT 38 pins: http://mh.nodebb.com/topic/2/mh-et-live-esp32-devkit
