# Fritzing sketch Fire_truck_Circuit (saved by Fritzing 0.8.7b)

parts:
  Part2 = Lilypad Power Supply
  S4 = Round Pushbutton
  MH-ET_LIVE_ESP32_DEVKIT2 = MH-ET LIVE ESP32 DEVKIT 38 pins
  LED5 = LED - 5mm [color="Red (633nm)" package="5 mm [THT]"]
  LED6 = LED - 5mm [color="White (4500K)" package="5 mm [THT]"]
  LED7 = LED - 5mm [color="Blue (470nm)" package="5 mm [THT]"]
  J3 = Piezo Speaker
  J4 = Piezo Speaker
  S5 = Pushbutton [package=THT]
  S6 = Pushbutton [package=THT]

nets:
  N1: Part2.+, MH-ET_LIVE_ESP32_DEVKIT2.5V
  N2: Part2.GND, MH-ET_LIVE_ESP32_DEVKIT2.GND#58, S6.leg0
  N3: S4.leg0, J3.pin1, J4.pin1
  N4: S4.leg1, MH-ET_LIVE_ESP32_DEVKIT2.IO17
  N5: MH-ET_LIVE_ESP32_DEVKIT2.IO12, J3.pin2
  N6: MH-ET_LIVE_ESP32_DEVKIT2.IO13, J4.pin2
  N7: MH-ET_LIVE_ESP32_DEVKIT2.GND#64, LED5.cathode
  N8: MH-ET_LIVE_ESP32_DEVKIT2.IO19, LED7.anode
  N9: MH-ET_LIVE_ESP32_DEVKIT2.IO18, S5.leg1
  N10: MH-ET_LIVE_ESP32_DEVKIT2.IO5, S6.leg1
  N11: MH-ET_LIVE_ESP32_DEVKIT2.IO16, LED6.anode
  N12: MH-ET_LIVE_ESP32_DEVKIT2.IO4, LED5.anode

custom parts:
  MH-ET LIVE ESP32 DEVKIT 38 pins: http://mh.nodebb.com/topic/2/mh-et-live-esp32-devkit
