# Fritzing sketch Spike_CIrcuit (saved by Fritzing 0.8.7b)

parts:
  MH-ET_LIVE_ESP32_DEVKIT1 = MH-ET LIVE ESP32 DEVKIT 38 pins
  J1 = Basic Servo
  Part1 = Lilypad Power Supply

nets:
  N1: MH-ET_LIVE_ESP32_DEVKIT1.GND#58, Part1.GND
  5V: MH-ET_LIVE_ESP32_DEVKIT1.5V, J1.vcc, Part1.+
  N2: MH-ET_LIVE_ESP32_DEVKIT1.GND#64, J1.gnd
  N3: MH-ET_LIVE_ESP32_DEVKIT1.IO17, J1.pulse

custom parts:
  MH-ET LIVE ESP32 DEVKIT 38 pins: http://mh.nodebb.com/topic/2/mh-et-live-esp32-devkit
