# Fritzing sketch Traffic_light_circuit (saved by Fritzing 0.8.7b)

parts:
  MH-ET_LIVE_ESP32_DEVKIT1 = MH-ET LIVE ESP32 DEVKIT 38 pins
  LED1 = LED - 5mm [color="Red (633nm)" package="5 mm [THT]"]
  LED2 = LED - 5mm [color="Yellow (592nm)" package="5 mm [THT]"]
  LED3 = LED - 5mm [color="Blue (430nm)" package="5 mm [THT]"]
  Part1 = Lilypad Power Supply

nets:
  N1: MH-ET_LIVE_ESP32_DEVKIT1.GND#58, Part1.GND
  N2: MH-ET_LIVE_ESP32_DEVKIT1.5V, Part1.+
  N3: MH-ET_LIVE_ESP32_DEVKIT1.GND#64, LED1.cathode
  N4: MH-ET_LIVE_ESP32_DEVKIT1.IO23, LED1.anode
  N5: MH-ET_LIVE_ESP32_DEVKIT1.IO22, LED2.anode
  N6: MH-ET_LIVE_ESP32_DEVKIT1.IO21, LED3.anode

custom parts:
  MH-ET LIVE ESP32 DEVKIT 38 pins: http://mh.nodebb.com/topic/2/mh-et-live-esp32-devkit
