# Fritzing sketch car1_circuit (saved by Fritzing 0.8.7b)

parts:
  S1 = Round Pushbutton
  MH-ET_LIVE_ESP32_DEVKIT1 = MH-ET LIVE ESP32 DEVKIT 38 pins
  LED1 = LED - 5mm [color="Blue (470nm)" package="5 mm [THT]"]
  LED2 = LED - 5mm [color="Red (633nm)" package="5 mm [THT]"]
  J1 = Piezo Speaker
  Part1 = Lilypad Power Supply
  LED3 = LED - 5mm [color="Green (555nm)" package="5 mm [THT]"]

nets:
  N1: S1.leg0, MH-ET_LIVE_ESP32_DEVKIT1.GND#64
  N2: S1.leg1, MH-ET_LIVE_ESP32_DEVKIT1.IO5
  N3: MH-ET_LIVE_ESP32_DEVKIT1.GND#58, J1.pin1, Part1.GND
  N4: MH-ET_LIVE_ESP32_DEVKIT1.IO13, J1.pin2
  N5: MH-ET_LIVE_ESP32_DEVKIT1.5V, Part1.+
  N6: MH-ET_LIVE_ESP32_DEVKIT1.GND#70, LED1.cathode, LED2.cathode
  N7: MH-ET_LIVE_ESP32_DEVKIT1.IO19, LED2.anode
  N8: MH-ET_LIVE_ESP32_DEVKIT1.IO16, LED3.cathode
  N9: MH-ET_LIVE_ESP32_DEVKIT1.IO4, LED1.anode

custom parts:
  MH-ET LIVE ESP32 DEVKIT 38 pins: http://mh.nodebb.com/topic/2/mh-et-live-esp32-devkit
